# Fritzing sketch UnoBuild (saved by Fritzing 0.9.0b)
circuit board: 8.46667cm x 5.64444cm
breadboards: 1

parts:
  Part1 = Arduino Uno (Rev3)
  Q2 = NPN-Transistor [package="TO92 [THT]"]
  Q4 = NPN-Transistor [package="TO92 [THT]"]
  VCC1 = Battery block 9V
  Part2 = SRF05 Ultrasonic Rangefinder
  Q5 = NPN-Transistor [package="TO92 [THT]"]
  R1 = Resistor [tolerance=±5% resistance=220 package=THT]
  R2 = Resistor [tolerance=±5% resistance=220 package=THT]
  R3 = Resistor [tolerance=±5% resistance=220 package=THT]
  LED2 = LED - 5mm [color="Red (633nm)" package="5 mm [THT]"]
  LED3 = LED - 5mm [color="Red (633nm)" package="5 mm [THT]"]
  LED4 = LED - 5mm [color="Red (633nm)" package="5 mm [THT]"]

nets:
  N1: Part1.D8, Q5.B
  N2: Part1.D12/MISO, Part2.Echo
  N3: Part1.D13/SCK, Q2.B
  N4: Part1.D4, Part2.Trig
  N5: Part1.D7, Q4.B
  5V: Part1.5V, Part2.VCC
  GND: Part1.GND, Q2.E, Q4.E, VCC1.-, Part2.GND, Q5.E
  N6: VCC1.+, R1.Pin_0, R2.Pin_0, R3.Pin_0
  N7: R1.Pin_1, LED3.cathode
  N8: R2.Pin_1, LED2.cathode
  N9: R3.Pin_1, LED4.cathode
